// Logisim project mARMiCPU.circ as structural Verilog: 10 circuits, main circuit main
module main (
);

  wire CLK, clock_1_out, cpu_1_halt, decimaldisplaycontrol_1_sign, frontpanelcontroller_1_runhalt, Reset,
       RunStop_out, Step_out;
  wire [3:0] cpu_1_aluflags, cpu_1_flags, decimaldisplaycontrol_1_d0, decimaldisplaycontrol_1_d1,
       decimaldisplaycontrol_1_d2, decimaldisplaycontrol_1_d3, decimaldisplaycontrol_1_d4, decimalio_1_data,
       decimalio_1_data_2, decimalio_1_data_3, decimalio_1_data_4;
  wire [15:0] cpu_1_alua, cpu_1_alub, cpu_1_aluresult, cpu_1_imaddress, cpu_1_imdata, cpu_1_writeback,
       DMAddress, DMData, IM_data;

  Clock clock_1 (.out(clock_1_out));
  ROM #(.addrWidth(16), .dataWidth(16)) IM (.addr(cpu_1_imaddress), .data(IM_data));
  FrontPanelController frontpanelcontroller_1 (
    .Clk(clock_1_out), .Run(RunStop_out), .Step(Step_out), .Reset(Reset), .Halt(cpu_1_halt), .CpuClk(CLK),
    .RunHalt(frontpanelcontroller_1_runhalt));
  CPU cpu_1 (
    .CLK(CLK), .Reset(Reset), .IMDataIn(IM_data), .Halt(cpu_1_halt), .IMAddress(cpu_1_imaddress),
    .IMData(cpu_1_imdata), .DMAddress(DMAddress), .DMData(DMData), .WriteBack(cpu_1_writeback),
    .Flags(cpu_1_flags), .AluA(cpu_1_alua), .AluB(cpu_1_alub), .ALUResult(cpu_1_aluresult),
    .ALUFlags(cpu_1_aluflags));
  LED led_1 (.in(cpu_1_flags[3]));
  LED led_2 (.in(cpu_1_flags[2]));
  LED led_3 (.in(cpu_1_flags[1]));
  LED led_4 (.in(cpu_1_flags[0]));
  Hex_Digit_Display hex_digit_display_1 (.value(cpu_1_alua[15:12]));  // open: dp
  LED led_5 (.in(cpu_1_halt));
  Hex_Digit_Display hex_digit_display_2 (.value(cpu_1_imaddress[15:12]));  // open: dp
  Hex_Digit_Display hex_digit_display_3 (.value(cpu_1_imaddress[11:8]));  // open: dp
  Hex_Digit_Display hex_digit_display_4 (.value(cpu_1_imdata[15:12]));  // open: dp
  Hex_Digit_Display hex_digit_display_5 (.value(cpu_1_imdata[11:8]));  // open: dp
  Hex_Digit_Display hex_digit_display_6 (.value(cpu_1_alua[11:8]));  // open: dp
  Hex_Digit_Display hex_digit_display_7 (.value(cpu_1_alua[7:4]));  // open: dp
  LED N (.in(cpu_1_aluflags[3]));
  LED Z (.in(cpu_1_aluflags[2]));
  LED C (.in(cpu_1_aluflags[1]));
  LED led_6 (.in(frontpanelcontroller_1_runhalt));
  Button RunStop (.out(RunStop_out));
  Hex_Digit_Display hex_digit_display_8 (.value(cpu_1_imaddress[7:4]));  // open: dp
  Hex_Digit_Display hex_digit_display_9 (.value(cpu_1_imaddress[3:0]));  // open: dp
  Hex_Digit_Display hex_digit_display_10 (.value(cpu_1_imdata[7:4]));  // open: dp
  // Hex_Digit_Display hex_digit_display_11: pin names not known; wires that end beside it: cpu_1_imdata[3:0]
  Hex_Digit_Display hex_digit_display_12 (.value(cpu_1_alua[3:0]));  // open: dp
  LED V (.in(cpu_1_aluflags[0]));
  Button Step (.out(Step_out));
  Hex_Digit_Display hex_digit_display_13 (.value(DMAddress[15:12]));  // open: dp
  Hex_Digit_Display hex_digit_display_14 (.value(DMData[15:12]));  // open: dp
  Hex_Digit_Display hex_digit_display_15 (.value(cpu_1_writeback[15:12]));  // open: dp
  Hex_Digit_Display hex_digit_display_16 (.value(cpu_1_alub[15:12]));  // open: dp
  Hex_Digit_Display hex_digit_display_17 (.value(cpu_1_aluresult[15:12]));  // open: dp
  Button u_Reset (.out(Reset));
  Hex_Digit_Display hex_digit_display_18 (.value(DMAddress[11:8]));  // open: dp
  Hex_Digit_Display hex_digit_display_19 (.value(DMAddress[7:4]));  // open: dp
  Hex_Digit_Display hex_digit_display_20 (.value(DMData[11:8]));  // open: dp
  Hex_Digit_Display hex_digit_display_21 (.value(DMData[7:4]));  // open: dp
  Hex_Digit_Display hex_digit_display_22 (.value(cpu_1_writeback[11:8]));  // open: dp
  Hex_Digit_Display hex_digit_display_23 (.value(cpu_1_writeback[7:4]));  // open: dp
  Hex_Digit_Display hex_digit_display_24 (.value(cpu_1_alub[11:8]));  // open: dp
  Hex_Digit_Display hex_digit_display_25 (.value(cpu_1_alub[7:4]));  // open: dp
  Hex_Digit_Display hex_digit_display_26 (.value(cpu_1_aluresult[11:8]));  // open: dp
  Hex_Digit_Display hex_digit_display_27 (.value(cpu_1_aluresult[7:4]));  // open: dp
  _7_Segment_Display u_7_segment_display_1 (.g(decimaldisplaycontrol_1_sign));  // open: f, a, b, e, d, c, dp
  Hex_Digit_Display hex_digit_display_28 (.value(DMAddress[3:0]));  // open: dp
  Hex_Digit_Display hex_digit_display_29 (.value(DMData[3:0]));  // open: dp
  Hex_Digit_Display hex_digit_display_30 (.value(cpu_1_writeback[3:0]));  // open: dp
  Hex_Digit_Display hex_digit_display_31 (.value(cpu_1_alub[3:0]));  // open: dp
  Hex_Digit_Display hex_digit_display_32 (.value(cpu_1_aluresult[3:0]));  // open: dp
  Hex_Digit_Display hex_digit_display_33 (.value(decimaldisplaycontrol_1_d4));  // open: dp
  Hex_Digit_Display hex_digit_display_34 (.value(decimaldisplaycontrol_1_d3));  // open: dp
  Hex_Digit_Display hex_digit_display_35 (.value(decimaldisplaycontrol_1_d2));  // open: dp
  Hex_Digit_Display hex_digit_display_36 (.value(decimalio_1_data_4));  // open: dp
  Hex_Digit_Display hex_digit_display_37 (.value(decimalio_1_data_3));  // open: dp
  Hex_Digit_Display hex_digit_display_38 (.value(decimaldisplaycontrol_1_d1));  // open: dp
  Hex_Digit_Display hex_digit_display_39 (.value(decimaldisplaycontrol_1_d0));  // open: dp
  DecimalDisplayControl decimaldisplaycontrol_1 (
    .DataIn({decimalio_1_data_4, decimalio_1_data_3, decimalio_1_data_2, decimalio_1_data}),
    .D0(decimaldisplaycontrol_1_d0), .D1(decimaldisplaycontrol_1_d1), .D2(decimaldisplaycontrol_1_d2),
    .D3(decimaldisplaycontrol_1_d3), .D4(decimaldisplaycontrol_1_d4), .sign(decimaldisplaycontrol_1_sign));
  DecimalIO decimalio_1 (
    .DMAddress(DMAddress), .DMData(DMData), .CLK(CLK), .Reset(Reset),
    .Data({decimalio_1_data_4, decimalio_1_data_3, decimalio_1_data_2, decimalio_1_data}));
  Hex_Digit_Display hex_digit_display_40 (.value(decimalio_1_data_2));  // open: dp
  Hex_Digit_Display hex_digit_display_41 (.value(decimalio_1_data));  // open: dp

  // Notes on the sheet:
  //   contents of IM (hex, n*v repeats v):
  //   8000 9fff a830 bf0e 2092 20da 1858 600
  //   N  Z  C  V
  //   Latched Flags
  //   HALT
  //   Instruction Memory
  //   mARMi
  //   ALU A Input
  //   ALU Flags
  //   Data Memory
  //   WriteBack
  //   ALU B Input
  //   ALU Result
endmodule

module CPU (
  input  CLK,
  input  Reset,
  input  [15:0] IMDataIn,
  output Halt,
  output [15:0] IMAddress,
  output [15:0] IMData,
  output [15:0] DMAddress,
  output [15:0] DMData,
  output [15:0] WriteBack,
  output [3:0] Flags,
  output [15:0] AluA,
  output [15:0] AluB,
  output [15:0] ALUResult,
  output [3:0] ALUFlags
);

  wire ALUSrc, CLKin, JMP, MaskA, MemWrite, not_1_out, RegSource, RegWrite;
  wire [1:0] MemtoReg;
  wire [2:0] A1final, multiplexer_1_out;
  wire [3:0] ALUControl;
  wire [15:0] bit_extender_2_out, DMData_t, ImmExtend, PCPlus1, RD1, registerfile8x16_1_rd2, WriteData;

  not not_1 (not_1_out, Halt);
  assign CLKin = not_1_out ? CLK : 1'bz;  // Controlled_Buffer controlled_buffer_1
  InstructionFetch instructionfetch_1 (
    .JMP(JMP), .WBBus(WriteBack), .CLK(CLKin), .Reset(Reset), .IMAddress(IMAddress), .PCPlus1(PCPlus1));
  DecoderController decodercontroller_1 (
    .IMData(IMDataIn), .ALUFlags(ALUFlags), .CLK(CLKin), .Reset(Reset), .ALUSrc(ALUSrc), .RegWrite(RegWrite),
    .RegSrc(RegSource), .ALUControl(ALUControl), .JMP(JMP), .MemWrite(MemWrite), .MemtoReg(MemtoReg),
    .Halt(Halt), .Flags(Flags), .MaskA(MaskA));
  Multiplexer #(.width(3)) multiplexer_1 (
    .in0(IMDataIn[5:3]), .in1(IMDataIn[14:12]), .out(multiplexer_1_out), .sel(IMDataIn[15]));
  Multiplexer #(.width(3)) multiplexer_2 (.in0(IMDataIn[8:6]), .in1(3'b111), .out(A1final), .sel(RegSource));
  assign ImmExtend = {{4{IMDataIn[11]}}, IMDataIn[11:0]};  // Bit_Extender bit_extender_1
  RegisterFile8x16 registerfile8x16_1 (
    .CLK(CLKin), .WE3(RegWrite), .A1(A1final), .A2(IMDataIn[2:0]), .A3(multiplexer_1_out), .WD3(WriteData),
    .R7(PCPlus1), .Reset(Reset), .RD1(RD1), .RD2(registerfile8x16_1_rd2), .RD3(DMData));
  Multiplexer #(.width(16)) multiplexer_3 (.in0(WriteBack), .in1(ImmExtend), .out(WriteData), .sel(IMDataIn[15]));
  Multiplexer #(.width(16)) multiplexer_4 (.in0(RD1), .in1({16{1'b0}}), .out(AluA), .sel(MaskA));
  Multiplexer #(.width(16)) multiplexer_5 (.in0(registerfile8x16_1_rd2), .in1(ImmExtend), .out(AluB), .sel(ALUSrc));
  assign bit_extender_2_out = {{12{1'b0}}, Flags};  // Bit_Extender bit_extender_2
  ALU alu_1 (.A(AluA), .B(AluB), .ALUOp(ALUControl), .Result(ALUResult), .FlagsNZCV(ALUFlags));
  Multiplexer #(.select(2), .width(16)) multiplexer_6 (
    .in0(ALUResult), .in1(DMData_t), .in2(RD1), .in3(bit_extender_2_out), .out(WriteBack), .sel(MemtoReg));
  DataMemory datamemory_1 (.DMAddress(ALUResult), .WE(MemWrite), .CLK(CLKin), .DMDataIn(DMData), .DMDataOut(DMData_t));

  assign DMAddress = ALUResult;
  assign IMData = IMDataIn;

  // Other names for the same wires on the sheet: A[15:0] = AluA; B[15:0] = AluB; DMDataIn[15:0] = DMData;
  //   A2[2:0] = IMDataIn[2:0]; A3[2:0] = IMDataIn[5:3]; A1[2:0] = IMDataIn[8:6]; IMData15 = IMDataIn[15];
  //   Result[15:0] = ALUResult

  // Notes on the sheet:
  //   CPU
endmodule

module FrontPanelController (
  input  Clk,
  input  Run,
  input  Step,
  input  Reset,
  input  Halt,
  output CpuClk,
  output RunHalt
);

  wire and_1_out, or_1_out, pull_resistor_1_node, t_ff_1_q;

  T_Flip_Flop t_ff_1 (.T(pull_resistor_1_node), .clk(Run), .Q(t_ff_1_q), .reset(Reset));  // open: Qn, preset
  Pull_Resistor #(.pull(1)) pull_resistor_1 (.node(pull_resistor_1_node));
  or or_1 (or_1_out, t_ff_1_q, Step);
  and and_1 (and_1_out, Clk, t_ff_1_q);
  and and_2 (RunHalt, or_1_out, ~Halt);  // AND_Gate
  Multiplexer multiplexer_1 (.in0(Step), .in1(and_1_out), .out(CpuClk), .sel(t_ff_1_q));
endmodule

module DecoderController (
  input  [15:0] IMData,
  input  [3:0] ALUFlags,
  input  CLK,
  input  Reset,
  output ALUSrc,
  output RegWrite,
  output RegSrc,
  output [3:0] ALUControl,
  output JMP,
  output MemWrite,
  output [1:0] MemtoReg,
  output Halt,
  output [3:0] Flags,
  output MaskA
);

  wire ALUOp, decoder_1_out2, decoder_1_out3, decoder_1_out4, decoder_1_out5, decoder_1_out6, decoder_1_out7,
       LDR, MovRdFlags, MovRdRn, NonALUOp, NOP, not_1_out, or_4_out, STR;

  Decoder #(.select(3)) decoder_1 (
    .out0(NonALUOp), .out1(ALUOp), .out2(decoder_1_out2), .out3(decoder_1_out3), .out4(decoder_1_out4),
    .out5(decoder_1_out5), .out6(decoder_1_out6), .out7(decoder_1_out7), .sel(IMData[15:13]));  // open: en
  or or_1 (RegSrc, decoder_1_out2, decoder_1_out3);
  or or_2 (MaskA, decoder_1_out4, decoder_1_out5, decoder_1_out6, decoder_1_out7);
  Register #(.width(4)) F (.D(ALUFlags), .en(ALUOp), .clk(CLK), .Q(Flags), .clr(Reset));
  Decoder #(.select(4)) decoder_2 (
    .out0(NOP), .out3(Halt), .out4(MovRdRn), .out5(MovRdFlags), .out8(LDR), .out12(STR), .sel(IMData[12:9]),
    .en(NonALUOp));  // open: out1, out2, out6, out7, out9, out10, out11, out13, out14, out15
  or or_3 (ALUSrc, MaskA, RegSrc);
  or or_4 (or_4_out, ALUOp, MaskA, MovRdFlags, MovRdRn, LDR);
  and and_1 (RegWrite, or_4_out, ~NOP);  // AND_Gate
  Multiplexer #(.width(4)) multiplexer_1 (.in0(4'b0000), .in1(IMData[12:9]), .out(ALUControl), .sel(ALUOp));
  not not_1 (not_1_out, Flags[2]);
  Multiplexer #(.enable("true"), .select(2)) multiplexer_2 (
    .in0(1'b1), .in1(1'b0), .in2(Flags[2]), .in3(not_1_out), .out(JMP), .sel(IMData[13:12]), .en(RegSrc));
  and and_2 (MemWrite, ~NOP, STR);  // AND_Gate
  or or_5 (MemtoReg[1], MovRdRn, MovRdFlags);
  or or_6 (MemtoReg[0], LDR, STR, MovRdFlags);
  // OR_Gate or_7 has open pins: in0=LDR, in1=RegSrc, in2=STR, out=open

  // Other names for the same wires on the sheet: i9 = IMData[9]; i10 = IMData[10]; i11 = IMData[11]; i12 = IMData[12];
  //   i13 = IMData[13]; Branch = RegSrc; V = Flags[0]; C = Flags[1]; Z = Flags[2]; N = Flags[3]; i0 = IMData[0];
  //   i1 = IMData[1]; i2 = IMData[2]; i3 = IMData[3]; i4 = IMData[4]; i5 = IMData[5]; i6 = IMData[6]; i7 = IMData[7];
  //   i8 = IMData[8]; i14 = IMData[14]; i15 = IMData[15]; MovRdImm = MaskA

  // Notes on the sheet:
  //   Main Instruction Decoder
  //   NonALUOp Decoder
endmodule

module InstructionFetch (
  input  JMP,
  input  [15:0] WBBus,
  input  CLK,
  input  Reset,
  output [15:0] IMAddress,
  output [15:0] PCPlus1
);

  wire [15:0] multiplexer_1_out;

  Register #(.width(16)) PC (.D(multiplexer_1_out), .en(1'b1), .clk(CLK), .Q(IMAddress), .clr(Reset));
  Multiplexer #(.width(16)) multiplexer_1 (.in0(PCPlus1), .in1(WBBus), .out(multiplexer_1_out), .sel(JMP));
  Adder #(.width(16)) adder_1 (.a(IMAddress), .b(16'h1), .out(PCPlus1));  // open: cin, cout

  // Notes on the sheet:
  //   Instruction Fetch
endmodule

module ALU (
  input  [15:0] A,
  input  [15:0] B,
  input  [3:0] ALUOp,
  output [15:0] Result,
  output [3:0] FlagsNZCV
);

  wire AddCarry, and_2_out, and_3_out, SubCarry, xnor_1_out, xor_2_out, xor_3_out;
  wire [15:0] adder_1_out, and_1_out, divider_1_out, divider_1_rem, multiplier_1_cout, multiplier_1_out,
       not_1_out, or_1_out, shifter_1_out, shifter_2_out, shifter_3_out, shifter_4_out, shifter_5_out,
       subtractor_1_out, xor_1_out;

  assign or_1_out = A | B;  // OR_Gate or_1, 16 bits wide
  assign and_1_out = A & B;  // AND_Gate and_1, 16 bits wide
  Divider #(.width(16)) divider_1 (.a(A), .b(B), .out(divider_1_out), .rem(divider_1_rem));  // open: upper
  Multiplier #(.width(16)) multiplier_1 (.a(A), .b(B), .out(multiplier_1_out), .cout(multiplier_1_cout));  // open: cin
  Subtractor #(.width(16)) subtractor_1 (.a(A), .b(B), .out(subtractor_1_out), .bout(SubCarry));  // open: bin
  Adder #(.width(16)) adder_1 (.a(A), .b(B), .out(adder_1_out), .cout(AddCarry));  // open: cin
  assign xor_1_out = A ^ B;  // XOR_Gate xor_1, 16 bits wide
  Multiplexer #(.select(4), .width(16)) multiplexer_1 (
    .in0(adder_1_out), .in1(subtractor_1_out), .in2(multiplier_1_out), .in3(multiplier_1_cout),
    .in4(divider_1_out), .in5(divider_1_rem), .in6(and_1_out), .in7(or_1_out), .in8(xor_1_out),
    .in9(not_1_out), .in10(shifter_1_out), .in11(shifter_2_out), .in12(shifter_3_out), .in13(shifter_4_out),
    .in14(shifter_5_out), .out({FlagsNZCV[3], Result[14:0]}), .sel(ALUOp));  // open: in15
  nor nor_1 (FlagsNZCV[2], FlagsNZCV[3], Result[14], Result[13], Result[12], Result[11], Result[10], Result[9], Result[8], Result[7], Result[6], Result[5], Result[4], Result[3], Result[2], Result[1], Result[0]);
  assign not_1_out = ~A;  // NOT_Gate not_1, 16 bits wide
  Shifter #(.width(16)) shifter_1 (.in(A), .\dist (B[3:0]), .out(shifter_1_out));
  Shifter #(.shift("lr"), .width(16)) shifter_2 (.in(A), .\dist (B[3:0]), .out(shifter_2_out));
  Shifter #(.shift("ar"), .width(16)) shifter_3 (.in(A), .\dist (B[3:0]), .out(shifter_3_out));
  Shifter #(.shift("rl"), .width(16)) shifter_4 (.in(A), .\dist (B[3:0]), .out(shifter_4_out));
  Shifter #(.shift("rr"), .width(16)) shifter_5 (.in(A), .\dist (B[3:0]), .out(shifter_5_out));
  xor xor_2 (xor_2_out, A[15], FlagsNZCV[3]);
  xnor xnor_1 (xnor_1_out, A[15], B[15]);
  and and_2 (and_2_out, xnor_1_out, xor_2_out);
  Multiplexer #(.select(4)) multiplexer_2 (
    .in0(AddCarry), .in1(SubCarry), .in2(1'b0), .in3(1'b0), .in4(1'b0), .in5(1'b0), .in6(1'b0), .in7(1'b0),
    .in8(1'b0), .in9(1'b0), .in10(1'b0), .in11(1'b0), .in12(1'b0), .in13(1'b0), .in14(1'b0),
    .out(FlagsNZCV[1]), .sel(ALUOp));  // open: in15
  xor xor_3 (xor_3_out, A[15], B[15]);
  and and_3 (and_3_out, xor_2_out, xor_3_out);
  Multiplexer #(.select(4)) multiplexer_3 (
    .in0(and_2_out), .in1(and_3_out), .in2(1'b0), .in3(1'b0), .in4(1'b0), .in5(1'b0), .in6(1'b0), .in7(1'b0),
    .in8(1'b0), .in9(1'b0), .in10(1'b0), .in11(1'b0), .in12(1'b0), .in13(1'b0), .in14(1'b0),
    .out(FlagsNZCV[0]), .sel(ALUOp));  // open: in15

  assign Result[15] = FlagsNZCV[3];

  // Other names for the same wires on the sheet: AMSB = A[15]; BMSB = B[15]; VFlag = FlagsNZCV[0];
  //   CFlag = FlagsNZCV[1]; ZFlag = FlagsNZCV[2]; NFlag = FlagsNZCV[3]; FourLSBB[3:0] = B[3:0]

  // Notes on the sheet:
  //   ALU
endmodule

module RegisterFile8x16 (
  input  CLK,
  input  WE3,
  input  [2:0] A1,
  input  [2:0] A2,
  input  [2:0] A3,
  input  [15:0] WD3,
  input  [15:0] R7,
  input  Reset,
  output [15:0] RD1,
  output [15:0] RD2,
  output [15:0] RD3
);

  wire demultiplexer_1_out0, demultiplexer_1_out1, demultiplexer_1_out2, demultiplexer_1_out3,
       demultiplexer_1_out4, demultiplexer_1_out5, demultiplexer_1_out6;
  wire [15:0] R0_q, R1_q, R2_q, R3_q, R4_q, R5_q, R6_q;

  Demultiplexer #(.select(3)) demultiplexer_1 (
    .out0(demultiplexer_1_out0), .out1(demultiplexer_1_out1), .out2(demultiplexer_1_out2),
    .out3(demultiplexer_1_out3), .out4(demultiplexer_1_out4), .out5(demultiplexer_1_out5),
    .out6(demultiplexer_1_out6), .in(WE3), .sel(A3));  // open: out7
  Register #(.width(16)) R0 (.D(WD3), .en(demultiplexer_1_out0), .clk(CLK), .Q(R0_q), .clr(Reset));
  Register #(.width(16)) R1 (.D(WD3), .en(demultiplexer_1_out1), .clk(CLK), .Q(R1_q), .clr(Reset));
  Register #(.width(16)) R2 (.D(WD3), .en(demultiplexer_1_out2), .clk(CLK), .Q(R2_q), .clr(Reset));
  Register #(.width(16)) R3 (.D(WD3), .en(demultiplexer_1_out3), .clk(CLK), .Q(R3_q), .clr(Reset));
  Register #(.width(16)) R4 (.D(WD3), .en(demultiplexer_1_out4), .clk(CLK), .Q(R4_q), .clr(Reset));
  Register #(.width(16)) R5 (.D(WD3), .en(demultiplexer_1_out5), .clk(CLK), .Q(R5_q), .clr(Reset));
  Register #(.width(16)) R6 (.D(WD3), .en(demultiplexer_1_out6), .clk(CLK), .Q(R6_q), .clr(Reset));
  Multiplexer #(.select(3), .width(16)) multiplexer_1 (
    .in0(R0_q), .in1(R1_q), .in2(R2_q), .in3(R3_q), .in4(R4_q), .in5(R5_q), .in6(R6_q), .in7(R7), .out(RD1),
    .sel(A1));
  Multiplexer #(.select(3), .width(16)) multiplexer_2 (
    .in0(R0_q), .in1(R1_q), .in2(R2_q), .in3(R3_q), .in4(R4_q), .in5(R5_q), .in6(R6_q), .in7(R7), .out(RD2),
    .sel(A2));
  Multiplexer #(.select(3), .width(16)) multiplexer_3 (
    .in0(R0_q), .in1(R1_q), .in2(R2_q), .in3(R3_q), .in4(R4_q), .in5(R5_q), .in6(R6_q), .in7(R7), .out(RD3),
    .sel(A3));

  // Notes on the sheet:
  //   Register File 
endmodule

module DataMemory (
  input  [15:0] DMAddress,
  input  WE,
  input  CLK,
  input  [15:0] DMDataIn,
  output [15:0] DMDataOut
);

  wire and_1_out, comparator_1_lt, not_1_out;

  Comparator #(.mode("unsigned"), .width(16)) comparator_1 (
    .a(DMAddress), .b(16'hf800), .lt(comparator_1_lt));  // open: gt, eq
  RAM #(.addrWidth(16), .asyncread("true"), .dataWidth(16)) DM (
    .addr(DMAddress), .we(and_1_out), .oe(not_1_out), .clk(CLK), .din(DMDataIn), .dout(DMDataOut));
  and and_1 (and_1_out, comparator_1_lt, WE);
  not not_1 (not_1_out, WE);

  // Notes on the sheet:
  //   Data Memory
endmodule

module DecimalDisplayControl (
  input  [15:0] DataIn,
  output [3:0] D0,
  output [3:0] D1,
  output [3:0] D2,
  output [3:0] D3,
  output [3:0] D4,
  output sign
);

  wire [15:0] adder_1_out, Binary, divider_1_out, divider_2_out, divider_3_out, divider_4_out, divider_5_out,
       not_1_out;
  wire [15:4] D0_t, D1_t, D2_t, D3_t, D4_t;

  assign not_1_out = ~DataIn;  // NOT_Gate not_1, 16 bits wide
  Divider #(.width(16)) divider_1 (.a(Binary), .b(16'ha), .out(divider_1_out), .rem({D0_t, D0}));  // open: upper
  Multiplexer #(.width(16)) multiplexer_1 (.in0(DataIn), .in1(adder_1_out), .out(Binary), .sel(DataIn[15]));
  Adder #(.width(16)) adder_1 (.a(not_1_out), .b(16'h1), .out(adder_1_out));  // open: cin, cout
  Divider #(.width(16)) divider_2 (.a(divider_1_out), .b(16'ha), .out(divider_2_out), .rem({D1_t, D1}));  // open: upper
  Divider #(.width(16)) divider_3 (.a(divider_2_out), .b(16'ha), .out(divider_3_out), .rem({D2_t, D2}));  // open: upper
  Divider #(.width(16)) divider_4 (.a(divider_3_out), .b(16'ha), .out(divider_4_out), .rem({D3_t, D3}));  // open: upper
  Divider #(.width(16)) divider_5 (.a(divider_4_out), .b(16'ha), .out(divider_5_out), .rem({D4_t, D4}));  // open: upper

  assign sign = DataIn[15];

  // Other names for the same wires on the sheet: D0_t[3:0] = D0; D1_t[3:0] = D1; D2_t[3:0] = D2; D3_t[3:0] = D3;
  //   D4_t[3:0] = D4; value[15:0] = DataIn

  // Notes on the sheet:
  //   Decimal Display Control
endmodule

module DecimalIO (
  input  [15:0] DMAddress,
  input  [15:0] DMData,
  input  CLK,
  input  Reset,
  output [15:0] Data
);

  wire WE;

  Register #(.width(16)) IO (.D(DMData), .en(WE), .clk(CLK), .Q(Data), .clr(Reset));
  Comparator #(.mode("unsigned"), .width(16)) comparator_1 (.a(DMAddress), .b({16{1'b1}}), .eq(WE));  // open: gt, lt

  // Notes on the sheet:
  //   Decimal IO
endmodule
